# Fritzing sketch Sensoreye Interative Sketch (saved by Fritzing 0.9.0b)
breadboards: 1

parts:
  Componente1 = Arduino Uno (Rev3) - ICSP
  Componente2 = SRF05 Ultrasonic Rangefinder
  R1 = Resistor [package="2010 [SMD]"]
  LED1 = smd LED [color="Red (633nm)" package="0805 [SMD]"]
  LED4 = smd LED [color="Red (633nm)" package="0805 [SMD]"]
  LED5 = smd LED [color="Yellow (585nm)" package="0805 [SMD]"]
  LED6 = smd LED [color="Yellow (585nm)" package="0805 [SMD]"]
  LED7 = smd LED [color="Green (555nm)" package="0805 [SMD]"]
  LED8 = smd LED [color="Green (555nm)" package="0805 [SMD]"]
  J1 = Piezo Speaker

nets:
  GND: Componente1.GND, Componente2.GND, LED1.cathode, LED4.cathode, LED5.cathode, LED6.cathode, LED7.cathode, LED8.cathode
  N1: Componente1.D9_PWM, R1.Pin_0, LED1.anode, LED4.anode, J1.pin1
  N2: Componente1.D12/MISO, Componente2.Echo
  N3: Componente1.D3_PWM, LED5.anode, LED6.anode
  N4: Componente1.D6_PWM, LED7.anode, LED8.anode
  N5: Componente1.D7, Componente2.Trig
  5V: Componente1.5V, Componente2.VCC
  N6: R1.Pin_1, J1.pin2
