# Fritzing sketch Sensoreye Sketch (saved by Fritzing 0.9.0b)

parts:
  Componente1 = Arduino Uno (Rev3) - ICSP
  Componente2 = SRF05 Ultrasonic Rangefinder
  VCC1 = Battery block 9V  # not connected
  U1 = Vibration Motor- ROB-08449 [package=vibe-motor-10mm]
  R1 = Resistor [tolerance=±5% resistance=220 package=THT]

nets:
  N1: Componente1.D11_PWM/MOSI, R1.Pin_0
  N2: Componente1.D12/MISO, Componente2.Echo
  N3: Componente1.D13/SCK, Componente2.Trig
  5V: Componente1.5V, Componente2.VCC
  GND: Componente1.GND, Componente2.GND, U1.+
  N4: U1.-, R1.Pin_1
